# Fritzing sketch neurawave (saved by Fritzing 0.9.10b)
breadboards: 1

parts:
  Part1 = Adafruit QT Py ESP32-C3 rev A
  S1 = SWITCH-MOMENTARY-2 [package=tactile_switch_tall]
  LED1 = LED - 5mm [color="Green (555nm)" current=0.030 package="5 mm [THT]"]
  R1 = Resistor [tolerance=±5% resistance=220 package="1206 [SMD]"]

nets:
  N1: Part1.A1, S1.1
  N2: Part1.GND, S1.2, LED1.cathode
  N3: LED1.anode, R1.Pin_0

notes:
  3.6V input
  VIN (Read)
  GND (Blue)
